# Fritzing sketch UltrasonicSimple (saved by Fritzing 0.9.3b)
breadboards: 1

parts:
  HC-SR04_Sensor_1 = HC-SR04 Ultrasonic Distance Sensor
  Componente1 = Arduino Uno (Rev3)
  LED1 = LED - 5mm [color="Red (633nm)" package="5 mm [THT]"]
  R1 = Resistor [tolerance=±5% resistance=220 package=THT]

nets:
  VCC: HC-SR04_Sensor_1.VCC, Componente1.5V
  N1: HC-SR04_Sensor_1.TRIG, Componente1.D12/MISO
  N2: HC-SR04_Sensor_1.ECHO, Componente1.D13/SCK
  GND: HC-SR04_Sensor_1.GND, Componente1.GND, R1.Pin_0
  N3: Componente1.D2, LED1.anode
  N4: LED1.cathode, R1.Pin_1
